# Fritzing sketch ANet LCD Wiring (saved by Fritzing 0.9.4)

parts:
  J1 = shrouded pin header, 10 pins [form="♂ (shrouded male)"]
  J2 = shrouded pin header, 10 pins [form="♂ (shrouded male)"]
  Part1 = Arduino Nano (Rev3.0)

nets:
  N1: J1.pin1, Part1.GND
  N2: J1.pin2, Part1.D10
  N3: J1.pin3, Part1.D11/MOSI
  N4: J1.pin5, Part1.D13/SCK
  N5: J1.pin6, Part1.D5
  N6: J1.pin7, Part1.D4
  N7: J1.pin8, Part1.D3
  N8: J1.pin9, Part1.D2
  N9: J1.pin10, Part1.5V
  N10: J2.pin4, Part1.D6

notes:
  U8G2_ST7920_128X64_F_SW_SPI u8g2(
  /* rotation */ U8G2_R0,
  /*clock=*/ 13,
  /*data=*/ 11,
  /*CS=*/ 10,
  /*reset=*/ U8X8_PIN_NONE
  );
