# Fritzing sketch Wiring (saved by Fritzing 0.9.4)

parts:
  J1 = male pin header, 7 pins [form="♂ (male)"]
  J2 = male pin header, 7 pins [form="♂ (male)"]
  U1 = MAX7219 [package=dil24]

nets:
  N1: J1.pin1, U1.DIG0
  N2: J1.pin2, U1.SEGE
  N3: J1.pin3, U1.SEGC
  N4: J1.pin4, U1.DIG2
  N5: J1.pin5, U1.SEGD
  N6: J1.pin7, U1.DIG4
  N7: J2.pin1, U1.SEGA
  N8: J2.pin2, U1.DIG1
  N9: J2.pin3, U1.SEGB
  N10: J2.pin5, U1.SEGF
  N11: J2.pin6, U1.DIG3
  N12: J2.pin7, U1.SEGG
