# Fritzing sketch RepRapDiscount_ All Connections (saved by Fritzing 0.9.4)

parts:
  J11 = shrouded pin header, 10 pins [form="♂ (shrouded male)"]
  LCD1 = LCD screen
  RE1 = Rotary Encoder [package=THT]  # not connected

nets:
  N1: J11.pin2, LCD1.E
  N2: J11.pin3, LCD1.DB4
  N3: J11.pin4, LCD1.DB6
  N4: J11.pin5, LCD1.VSS
  N5: J11.pin6, LCD1.VDD
  N6: J11.pin7, LCD1.DB7
  N7: J11.pin8, LCD1.DB5
  N8: J11.pin9, LCD1.RS
