# Fritzing sketch RepRapDiscount_LCD backpack (saved by Fritzing 0.9.4)

parts:
  LCM1602_IIC5 = LCM1602 IIC [part_number="LCM1602 IIC" chip_label="LCM1602 IIC" package="DIP (Dual Inline) [THT]"]
  J11 = shrouded pin header, 10 pins [form="♂ (shrouded male)"]
  U1 = ESP32S-HiLetgo [part_number=ESP32S-HiLetgo]
  Part3 = I2C level shifter bidirectional

nets:
  N1: LCM1602_IIC5.VSS, J11.pin5
  N2: LCM1602_IIC5.VDD, J11.pin6
  N3: LCM1602_IIC5.RS, J11.pin9
  N4: LCM1602_IIC5.E, J11.pin2
  N5: LCM1602_IIC5.D4, J11.pin3
  N6: LCM1602_IIC5.D5, J11.pin8
  N7: LCM1602_IIC5.D6, J11.pin4
  N8: LCM1602_IIC5.D7, J11.pin7
  GND: LCM1602_IIC5.GND, U1.GND, Part3.GND
  VCC: LCM1602_IIC5.VCC, U1.VIN, Part3.HV
  N9: LCM1602_IIC5.SDA, Part3.HV2
  N10: LCM1602_IIC5.SCL, Part3.HV1
  N11: U1.3.3, Part3.LV
  N12: U1.GPIO21, Part3.LV2
  N13: U1.GPIO22, Part3.LV1

custom parts:
  LCM1602 IIC: I2C-Module to use a 1602 or 2004 LCD on with the wire.h libory Serial LCD Modul
  ESP32S-HiLetgo: HiLetgo ESP-WROOM-32 ESP32 ESP-32S Development Board 2.4GHz Dual-Mode WiFi + Bluetooth Dual Cores Microcontroller The ESP32 integrated with Antenna switches, RF Balun, power amplifiers, low-noise amplifiers, filters, and management modules, and the entire solution occupies the least area of PCB. 2.4 GHz Wi-Fi plus Bluetooth dual-mode chip, with TSMC Ultra-low power consumption 40nm technology,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
