# Fritzing sketch RepRepDiscount (saved by Fritzing 0.9.4)

parts:
  J1 = shrouded pin header, 10 pins [form="♂ (shrouded male)"]
  J2 = shrouded pin header, 10 pins [form="♂ (shrouded male)"]
  J3 = female pin header, 5 pins [form="♀ (female)"]
  J4 = female pin header, 5 pins [form="♀ (female)"]
  J3_2 = female pin header, 5 pins [form="♀ (female)"]
  J5 = female pin header, 5 pins [form="♀ (female)"]
  J6 = female pin header, 5 pins [form="♀ (female)"]
  J7 = female pin header, 5 pins [form="♀ (female)"]
  J8 = female pin header, 5 pins [form="♀ (female)"]
  J9 = female pin header, 5 pins [form="♀ (female)"]
  J10 = shrouded pin header, 10 pins [form="♂ (shrouded male)"]
  J11 = shrouded pin header, 10 pins [form="♂ (shrouded male)"]
  LCD2 = LCD screen  # not connected
  J12 = female pin header, 16 pins [form="♀ (female)"]  # not connected
  LCM1602_IIC2 = LCM1602 IIC [part_number="LCM1602 IIC" chip_label="LCM1602 IIC" package="DIP (Dual Inline) [THT]"]  # not connected
  LCM1602_IIC3 = LCM1602 IIC [part_number="LCM1602 IIC" chip_label="LCM1602 IIC" package="DIP (Dual Inline) [THT]"]  # not connected
  LCM1602_IIC4 = LCM1602 IIC [part_number="LCM1602 IIC" chip_label="LCM1602 IIC" package="DIP (Dual Inline) [THT]"]

nets:
  N1: J1.pin1, J5.pin1
  N2: J1.pin2, J5.pin2
  N3: J1.pin3, J5.pin3
  N4: J1.pin4, J5.pin4
  N5: J1.pin5, J5.pin5
  N6: J1.pin6, J3_2.pin5
  N7: J1.pin7, J3_2.pin4
  N8: J1.pin8, J3_2.pin3
  N9: J1.pin9, J3_2.pin2
  N10: J1.pin10, J3_2.pin1
  N11: J2.pin1, J3.pin1
  N12: J2.pin2, J3.pin2
  N13: J2.pin3, J3.pin3
  N14: J2.pin4, J3.pin4
  N15: J2.pin7, J4.pin4
  N16: J2.pin8, J4.pin3
  N17: J2.pin9, J4.pin2
  N18: J2.pin10, J4.pin1
  N19: J6.pin1, J11.pin1
  N20: J6.pin2, J11.pin2
  N21: J6.pin3, J11.pin3
  N22: J6.pin4, J11.pin4
  N23: J7.pin1, J11.pin10
  N24: J7.pin2, J11.pin9
  N25: J7.pin3, J11.pin8
  N26: J7.pin4, J11.pin7
  N27: J8.pin1, J10.pin10
  N28: J8.pin2, J10.pin9
  N29: J8.pin3, J10.pin8
  N30: J8.pin4, J10.pin7
  N31: J9.pin1, J10.pin1
  N32: J9.pin2, J10.pin2
  N33: J9.pin3, J10.pin3
  N34: J9.pin4, J10.pin4
  N35: J11.pin5, LCM1602_IIC4.VSS
  N36: J11.pin6, LCM1602_IIC4.VDD

notes:
  Pin number labels on the PCB are often bonkers (and sometimes the connector has been inserted upside down!), so go by position, as viewed from the back of the board, as below:
  Exp1:
  Enc.Sw | RS | D5 | D7 | 5V
  Grey | Yellow | White| White| Red
  -------------------------------------------------
  Buzzer | Enable | D4 | D6 | GND
  Purple | Blue | White |White| Black
  Exp2:
  CLK | CS/SS | DIn (MOSI | Btn | NC
  Yellow | White | Blue | Grey | -
  ----------------------------------------------------
  DOut (MISO) | Enc.A | Enc.B | SD DETECT | NC
  Green | Yellow | Yellow | Brown | -
  https://forum.arduino.cc/t/how-to-use-reprapdiscount-smart-controller/535246/27

custom parts:
  LCM1602 IIC: I2C-Module to use a 1602 or 2004 LCD on with the wire.h libory Serial LCD Modul
