# Fritzing sketch ANet LCD12864 Wiring (saved by Fritzing 0.9.4)

parts:
  J1 = shrouded pin header, 10 pins [form="♂ (shrouded male)"]
  J2 = shrouded pin header, 10 pins [form="♂ (shrouded male)"]
  Part1 = Arduino Nano (Rev3.0)

nets:
  N1: J1.pin1, Part1.GND
  N2: J1.pin2, Part1.D10
  N3: J1.pin3, Part1.D11/MOSI
  N4: J1.pin5, Part1.D13/SCK
  N5: J1.pin6, Part1.D5
  N6: J1.pin7, Part1.D4
  N7: J1.pin8, Part1.D3
  N8: J1.pin9, Part1.D2
  N9: J1.pin10, Part1.5V
  N10: J2.pin4, Part1.D6

notes:
  U8G2_ST7920_128X64_F_SW_SPI u8g2(
  /* rotation */ U8G2_R0,
  /*clock=*/ 13,
  /*data=*/ 11,
  /*CS=*/ 10,
  /*reset=*/ U8X8_PIN_NONE
  );
  LCD Connector (Note tab is at bottom)
  ---
  |2|4|6|8|10|
  |1|3|5|7| 9 |
  1) GND (Black)
  2) +5V (Red)
  3) CS (White)
  4) Rotary Encoder 1
  5) MOSI (Green)
  6) Rotary Encoder 2
  7) -
  8) Rotary Encoder Click
  9) CLK (Yellow)
  10) Buzzer (Purple)
  J3 Connector (Note tab is at bottom)
  ---
  |2|4|6|8|10|
  |1|3|5|7| 9 |
  7) Button
