# Fritzing sketch HP 5082-7414 Bubble Display (saved by Fritzing 0.9.4)

parts:
  U1 = MAX7219 [package=dil24]
  J1 = male pin header, 7 pins [form="♂ (male)"]
  J2 = male pin header, 7 pins [form="♂ (male)"]
  Part1 = Arduino Nano (Rev3.0)
  R1 = Resistor [tolerance=±5% resistance=68k package=THT]
  C1 = Ceramic Capacitor [capacitance=100nF package="100 mil [THT, multilayer]"]

nets:
  N1: U1.DIN, Part1.D11/MOSI
  N2: U1.DIG0, J1.pin1
  N3: U1.DIG4, J1.pin7
  GND: U1.GND, U1.GND2, Part1.GND, C1.0
  N4: U1.DIG2, J1.pin4
  N5: U1.DIG3, J2.pin6
  N6: U1.DIG1, J2.pin2
  N7: U1.LOAD, Part1.D10
  N8: U1.CLK, Part1.D13/SCK
  N9: U1.SEGA, J2.pin1
  N10: U1.SEGF, J2.pin5
  N11: U1.SEGB, J2.pin3
  N12: U1.SEGG, J2.pin7
  N13: U1.ISET, R1.Pin_1
  VCC: U1.VCC, Part1.5V, R1.Pin_0, C1.1
  N14: U1.SEGC, J1.pin3
  N15: U1.SEGE, J1.pin2
  N16: U1.SEGDP, J1.pin5
  N17: U1.SEGD, J1.pin6

notes:
  HP 5082-7415
  According to https://www.datasheets360.com/part/detail/5082-7414/-6482069211030632702/
  Forward Current 5mA
  Forward Voltage 2.0V
  So need Rset on MAX7219 of >40k to limit current
  5082-7415 Pinout
  ---
  1 Cathode 1 14 Anode a
  2 Anode e 13 Cathode 2
  3 Anode c 12 Anode b
  4 Cathode 3 11 n/c
  5 Anode d.p. 10 Anode f
  6 Anode d 9 Cathode 4
  7 Cathode 5 8 Anode g
