# Fritzing sketch LCD12864 Wiring (saved by Fritzing 0.9.4)

parts:
  GLCD_128x1 = 128 x 64 Graphic LCD
  R1 = Resistor [tolerance=±5% resistance=220 package=THT]
  R2 = Rotary Potentiometer (Large) [maximum_resistance=100kΩ package=THT]
  Part1 = Arduino Uno (Rev3)
  R3 = Resistor [tolerance=±5% resistance=220 package=THT]
  R4 = Rotary Potentiometer (Large) [maximum_resistance=100kΩ package=THT]
  GLCD_128x2 = 128 x 64 Graphic LCD
  U1 = ESP32S-HiLetgo [part_number=ESP32S-HiLetgo]

nets:
  N1: GLCD_128x1.1_Vss, GLCD_128x1.15_CS1, GLCD_128x1.20_K(-), R2.leg2, Part1.GND
  N2: GLCD_128x1.2_Vdd, R1.Pin_1, R2.leg1, Part1.5V
  N3: GLCD_128x1.3_Vo, R2.wiper
  N4: GLCD_128x1.4_D/I, Part1.D10_PWM/SS
  N5: GLCD_128x1.5_R/W, Part1.D11_PWM/MOSI
  N6: GLCD_128x1.6_Enable, Part1.D13/SCK
  N7: GLCD_128x1.19_A(+), R1.Pin_0
  N8: R3.Pin_0, GLCD_128x2.19_A(+)
  N9: R3.Pin_1, R4.leg1, GLCD_128x2.2_Vdd, U1.VIN
  N10: R4.wiper, GLCD_128x2.3_Vo
  N11: R4.leg2, GLCD_128x2.1_Vss, GLCD_128x2.15_CS1, GLCD_128x2.20_K(-), U1.3.3, U1.GND
  N12: GLCD_128x2.4_D/I, U1.GPIO5
  N13: GLCD_128x2.5_R/W, U1.GPIO22, U1.GPIO23
  N14: GLCD_128x2.6_Enable, U1.GPIO18

notes:
  10k linear pot (optional) between GND and Vdd, with wiper to Vo allows adjustable contrast
  To use the LCD in SERIAL mode, connect the PSB pin (here labelled CS1) to GND, and then use an SPI interface as follows:
  Label A.K.A. Arduino ESP32
  D/I SS 10 5
  R/W MOSI 11 23
  E CLK 13 18
  Note: 5V and GND for LCD backlight (or 3.3V).
  Note that resistor may not be required if one is already soldered to the reverse of the board.
  Reset (optional)
  Note: The ST7920 chip itself operates from 2.7V to 5.5V BUT the crystals require ~5V on Vdd. According to the specs Logic HIGH is 0.7×Vdd, which would suggest 3.5V but, in practice, a 3.3V signal will still be accepted as Logic HIGH on the SPI pins, so we do not need a level shifter.
  Label A.K.A. Arduino ESP32
  D/I SS 10 5
  R/W MOSI 11 23
  E CLK 13 18
  5V Arduino
  3.3V ESP32

custom parts:
  ESP32S-HiLetgo: HiLetgo ESP-WROOM-32 ESP32 ESP-32S Development Board 2.4GHz Dual-Mode WiFi + Bluetooth Dual Cores Microcontroller The ESP32 integrated with Antenna switches, RF Balun, power amplifiers, low-noise amplifiers, filters, and management modules, and the entire solution occupies the least area of PCB. 2.4 GHz Wi-Fi plus Bluetooth dual-mode chip, with TSMC Ultra-low power consumption 40nm technology,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
