# Fritzing sketch MH-ET LIVE e-paper Wiring (saved by Fritzing 0.9.4)

parts:
  J1 = female pin header, 8 pins [form="♀ (female)"]
  U1 = ESP32S-HiLetgo [part_number=ESP32S-HiLetgo]

nets:
  N1: J1.pin1, U1.GPIO32
  N2: J1.pin2, U1.GPIO27
  N3: J1.pin3, U1.GPIO26
  N4: J1.pin4, U1.GPIO5
  N5: J1.pin5, U1.GPIO18
  N6: J1.pin6, U1.GPIO23
  N7: J1.pin7, U1.GND
  N8: J1.pin8, U1.3.3

notes:
  Busy (Purple) 32
  Reset (Grey) 27
  (Data/Command) D/C 26
  CS (White) 5
  SCLK (Yellow) 18
  SDI (MOSI) (Blue) 23
  GND (Black)
  VCC (Red) 3.3V
  Using the GxEPD2 library, this board can be initialised as
  GxEPD2_3C<GxEPD2_290c, GxEPD2_290c::HEIGHT> display(GxEPD2_290c(/*CS=5*/ SS, /*DC=*/ 26, /*RST=*/ 27, /*BUSY=*/ 32)); // GDEW029Z10

custom parts:
  ESP32S-HiLetgo: HiLetgo ESP-WROOM-32 ESP32 ESP-32S Development Board 2.4GHz Dual-Mode WiFi + Bluetooth Dual Cores Microcontroller The ESP32 integrated with Antenna switches, RF Balun, power amplifiers, low-noise amplifiers, filters, and management modules, and the entire solution occupies the least area of PCB. 2.4 GHz Wi-Fi plus Bluetooth dual-mode chip, with TSMC Ultra-low power consumption 40nm technology,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
